# Fritzing sketch cartao_ponto (saved by Fritzing 0.9.6b)
breadboards: 1

parts:
  Componente1 = Arduino Ethernet Shield (Rev3)
  LED1 = smd LED [color="Yellow (595nm)" package="0603 [SMD]"]
  LED2 = smd LED [color="Red (633nm)" package="0603 [SMD]"]
  LED3 = smd LED [color="Green (565nm)" package="0603 [SMD]"]
  S4 = Momentary Switch [package=ksa_sealed_tac_switch]
  R1 = Resistor [tolerance=±5% resistance=220 package="0402 [SMD]"]
  R2 = Resistor [tolerance=±5% resistance=220 package="0805 [SMD]"]
  R3 = Resistor [tolerance=±5% resistance=220 package="0805 [SMD]"]
  J1 = Piezo Speaker
  Grove1 = Grove OLED 128x96
  Componente2 = RFID USB Reader

nets:
  N1: Componente1.D8, Componente2.GNDT
  N2: Componente1.PWM_D9, Componente2.GND
  N3: Componente1.PWM_D11, Componente2.ANT2
  N4: Componente1.SPI/D12, Componente2.ANT1
  N5: Componente1.SPI/D13, Componente2.CP
  N6: Componente1.A4/SDA, Grove1.SDA
  N7: Componente1.A5/SCL, Grove1.SCL
  N8: Componente1.D2, J1.pin2
  N9: Componente1.PWM_D3, S4.3
  N10: Componente1.PWM_D5, R1.Pin_0
  N11: Componente1.PWM_D6, R3.Pin_0
  N12: Componente1.D7, R2.Pin_0
  3V3: Componente1.3V3, Componente2.VCC
  5V: Componente1.5V, Grove1.VCC, Componente2.TX-O
  GND: Componente1.GND, LED1.cathode, LED2.cathode, LED3.cathode, S4.1, J1.pin1, Grove1.GND
  N13: LED1.anode, R3.Pin_1
  N14: LED2.anode, R2.Pin_1
  N15: LED3.anode, R1.Pin_1

notes:
  baixo cima
